// Logisim project calculatorCPU.circ as structural Verilog: 15 circuits, main circuit main
module main (
);

  wire _0_out, _1_out, _2_out, _3_out, _4_out, _5_out, _6_out, _7_out, _8_out, _9_out, button_2_out,
       button_3_out, button_4_out, button_5_out, button_out, C_out, KEYPAD_CONTROLLER_write;
  wire [2:0] LCD_CONTROLLER__7_segment_3_2, LCD_CONTROLLER__7_segment_4_2, LCD_CONTROLLER__7_segment_5_2,
       LCD_CONTROLLER__7_segment_6_2, LCD_CONTROLLER__7_segment_7_2, LCD_CONTROLLER__7_segment_8_2,
       LCD_CONTROLLER__7_segment_9_2, LCD_CONTROLLER_minus_2;
  wire [3:0] LCD_CONTROLLER__7_segment_3, LCD_CONTROLLER__7_segment_4, LCD_CONTROLLER__7_segment_5,
       LCD_CONTROLLER__7_segment_6, LCD_CONTROLLER__7_segment_7, LCD_CONTROLLER__7_segment_8,
       LCD_CONTROLLER__7_segment_9, LCD_CONTROLLER_minus;
  wire [6:0] LCD_CONTROLLER__7_segment_0, LCD_CONTROLLER__7_segment_1, LCD_CONTROLLER__7_segment_2;
  wire [31:0] cpu_1_from_t8, cpu_1_from_t9, KEYPAD_CONTROLLER_output;

  // Probe on cpu_1_from_t9
  // Probe on KEYPAD_CONTROLLER_output
  // Probe on KEYPAD_CONTROLLER_write
  // Probe on cpu_1_from_t8
  CPU cpu_1 (
    .Write_to__t9(KEYPAD_CONTROLLER_output), .Write_To_Keyboard(KEYPAD_CONTROLLER_write),
    .from_t8(cpu_1_from_t8), .from_t9(cpu_1_from_t9));
  _7_Segment_Display u_7_segment_display_1 (
    .g(LCD_CONTROLLER__7_segment_9[0]), .f(LCD_CONTROLLER__7_segment_9[1]),
    .a(LCD_CONTROLLER__7_segment_9[2]), .b(LCD_CONTROLLER__7_segment_9[3]),
    .e(LCD_CONTROLLER__7_segment_9_2[0]), .d(LCD_CONTROLLER__7_segment_9_2[1]),
    .c(LCD_CONTROLLER__7_segment_9_2[2]));  // open: dp
  _7_Segment_Display u_7_segment_display_2 (
    .g(LCD_CONTROLLER_minus[0]), .f(LCD_CONTROLLER_minus[1]), .a(LCD_CONTROLLER_minus[2]),
    .b(LCD_CONTROLLER_minus[3]), .e(LCD_CONTROLLER_minus_2[0]), .d(LCD_CONTROLLER_minus_2[1]),
    .c(LCD_CONTROLLER_minus_2[2]));  // open: dp
  LCD_Controller LCD_CONTROLLER (
    .From__t8(cpu_1_from_t8), .Minus({LCD_CONTROLLER_minus_2, LCD_CONTROLLER_minus}),
    ._7_Segment_9({LCD_CONTROLLER__7_segment_9_2, LCD_CONTROLLER__7_segment_9}),
    ._7_Segment_8({LCD_CONTROLLER__7_segment_8_2, LCD_CONTROLLER__7_segment_8}),
    ._7_Segment_7({LCD_CONTROLLER__7_segment_7_2, LCD_CONTROLLER__7_segment_7}),
    ._7_Segment_6({LCD_CONTROLLER__7_segment_6_2, LCD_CONTROLLER__7_segment_6}),
    ._7_Segment_5({LCD_CONTROLLER__7_segment_5_2, LCD_CONTROLLER__7_segment_5}),
    ._7_Segment_4({LCD_CONTROLLER__7_segment_4_2, LCD_CONTROLLER__7_segment_4}),
    ._7_Segment_3({LCD_CONTROLLER__7_segment_3_2, LCD_CONTROLLER__7_segment_3}),
    ._7_Segment_2(LCD_CONTROLLER__7_segment_2), ._7_Segment_1(LCD_CONTROLLER__7_segment_1),
    ._7_Segment_0(LCD_CONTROLLER__7_segment_0));
  Keypad_Controller KEYPAD_CONTROLLER (
    .C(C_out), .in_2(button_out), .in_3(button_5_out), .in_4(button_4_out), .in_5(button_3_out),
    .in_6(button_2_out), ._9(_9_out), ._8(_8_out), ._7(_7_out), ._6(_6_out), ._5(_5_out), ._4(_4_out),
    ._3(_3_out), ._2(_2_out), ._1(_1_out), ._0(_0_out), .From__t9(cpu_1_from_t9),
    .Write(KEYPAD_CONTROLLER_write), .Output(KEYPAD_CONTROLLER_output));
  _7_Segment_Display u_7_segment_display_3 (
    .g(LCD_CONTROLLER__7_segment_8[0]), .f(LCD_CONTROLLER__7_segment_8[1]),
    .a(LCD_CONTROLLER__7_segment_8[2]), .b(LCD_CONTROLLER__7_segment_8[3]),
    .e(LCD_CONTROLLER__7_segment_8_2[0]), .d(LCD_CONTROLLER__7_segment_8_2[1]),
    .c(LCD_CONTROLLER__7_segment_8_2[2]));  // open: dp
  _7_Segment_Display u_7_segment_display_4 (
    .g(LCD_CONTROLLER__7_segment_7[0]), .f(LCD_CONTROLLER__7_segment_7[1]),
    .a(LCD_CONTROLLER__7_segment_7[2]), .b(LCD_CONTROLLER__7_segment_7[3]),
    .e(LCD_CONTROLLER__7_segment_7_2[0]), .d(LCD_CONTROLLER__7_segment_7_2[1]),
    .c(LCD_CONTROLLER__7_segment_7_2[2]));  // open: dp
  _7_Segment_Display u_7_segment_display_5 (
    .g(LCD_CONTROLLER__7_segment_5[0]), .f(LCD_CONTROLLER__7_segment_5[1]),
    .a(LCD_CONTROLLER__7_segment_5[2]), .b(LCD_CONTROLLER__7_segment_5[3]),
    .e(LCD_CONTROLLER__7_segment_5_2[0]), .d(LCD_CONTROLLER__7_segment_5_2[1]),
    .c(LCD_CONTROLLER__7_segment_5_2[2]));  // open: dp
  _7_Segment_Display u_7_segment_display_6 (
    .g(LCD_CONTROLLER__7_segment_6[0]), .f(LCD_CONTROLLER__7_segment_6[1]),
    .a(LCD_CONTROLLER__7_segment_6[2]), .b(LCD_CONTROLLER__7_segment_6[3]),
    .e(LCD_CONTROLLER__7_segment_6_2[0]), .d(LCD_CONTROLLER__7_segment_6_2[1]),
    .c(LCD_CONTROLLER__7_segment_6_2[2]));  // open: dp
  Button _7 (.out(_7_out));
  Button _4 (.out(_4_out));
  Button _1 (.out(_1_out));
  Button _0 (.out(_0_out));
  _7_Segment_Display u_7_segment_display_7 (
    .g(LCD_CONTROLLER__7_segment_4[0]), .f(LCD_CONTROLLER__7_segment_4[1]),
    .a(LCD_CONTROLLER__7_segment_4[2]), .b(LCD_CONTROLLER__7_segment_4[3]),
    .e(LCD_CONTROLLER__7_segment_4_2[0]), .d(LCD_CONTROLLER__7_segment_4_2[1]),
    .c(LCD_CONTROLLER__7_segment_4_2[2]));  // open: dp
  _7_Segment_Display u_7_segment_display_8 (
    .g(LCD_CONTROLLER__7_segment_3[0]), .f(LCD_CONTROLLER__7_segment_3[1]),
    .a(LCD_CONTROLLER__7_segment_3[2]), .b(LCD_CONTROLLER__7_segment_3[3]),
    .e(LCD_CONTROLLER__7_segment_3_2[0]), .d(LCD_CONTROLLER__7_segment_3_2[1]),
    .c(LCD_CONTROLLER__7_segment_3_2[2]));  // open: dp
  Button _8 (.out(_8_out));
  Button _5 (.out(_5_out));
  Button _2 (.out(_2_out));
  Button C (.out(C_out));
  _7_Segment_Display u_7_segment_display_9 (
    .g(LCD_CONTROLLER__7_segment_2[0]), .f(LCD_CONTROLLER__7_segment_2[1]),
    .a(LCD_CONTROLLER__7_segment_2[2]), .b(LCD_CONTROLLER__7_segment_2[3]),
    .e(LCD_CONTROLLER__7_segment_2[4]), .d(LCD_CONTROLLER__7_segment_2[5]), .c(LCD_CONTROLLER__7_segment_2[6]));  // open: dp
  _7_Segment_Display u_7_segment_display_10 (
    .g(LCD_CONTROLLER__7_segment_1[0]), .f(LCD_CONTROLLER__7_segment_1[1]),
    .a(LCD_CONTROLLER__7_segment_1[2]), .b(LCD_CONTROLLER__7_segment_1[3]),
    .e(LCD_CONTROLLER__7_segment_1[4]), .d(LCD_CONTROLLER__7_segment_1[5]), .c(LCD_CONTROLLER__7_segment_1[6]));  // open: dp
  Button _9 (.out(_9_out));
  Button _6 (.out(_6_out));
  Button _3 (.out(_3_out));
  Button button (.out(button_out));
  _7_Segment_Display u_7_segment_display_11 (
    .g(LCD_CONTROLLER__7_segment_0[0]), .f(LCD_CONTROLLER__7_segment_0[1]),
    .a(LCD_CONTROLLER__7_segment_0[2]), .b(LCD_CONTROLLER__7_segment_0[3]),
    .e(LCD_CONTROLLER__7_segment_0[4]), .d(LCD_CONTROLLER__7_segment_0[5]), .c(LCD_CONTROLLER__7_segment_0[6]));  // open: dp
  Button button_2 (.out(button_2_out));
  Button button_3 (.out(button_3_out));
  Button button_4 (.out(button_4_out));
  Button button_5 (.out(button_5_out));

  // Notes on the sheet:
  //   Kerilee Bookleiner
  //   probes to test
  //   From $t8
  //   From $t9
  //   Write Data to $t9
  //   Write Signal for $t9
endmodule

module LCD_Controller (
  input  [31:0] From__t8,
  output [6:0] Minus,
  output [6:0] _7_Segment_9,
  output [6:0] _7_Segment_8,
  output [6:0] _7_Segment_7,
  output [6:0] _7_Segment_6,
  output [6:0] _7_Segment_5,
  output [6:0] _7_Segment_4,
  output [6:0] _7_Segment_3,
  output [6:0] _7_Segment_2,
  output [6:0] _7_Segment_1,
  output [6:0] _7_Segment_0
);

  wire [3:0] binarytobcd_1_bcd0, binarytobcd_1_bcd1, binarytobcd_1_bcd2, binarytobcd_1_bcd3,
       binarytobcd_1_bcd4, binarytobcd_1_bcd5, binarytobcd_1_bcd6, binarytobcd_1_bcd7, binarytobcd_1_bcd8,
       binarytobcd_1_bcd9;

  BinaryToBCD binarytobcd_1 (
    .Minus(Minus[0]), .Input(From__t8), .BCD9(binarytobcd_1_bcd9), .BCD8(binarytobcd_1_bcd8),
    .BCD7(binarytobcd_1_bcd7), .BCD6(binarytobcd_1_bcd6), .BCD5(binarytobcd_1_bcd5),
    .BCD4(binarytobcd_1_bcd4), .BCD3(binarytobcd_1_bcd3), .BCD2(binarytobcd_1_bcd2),
    .BCD1(binarytobcd_1_bcd1), .BCD0(binarytobcd_1_bcd0));
  _7_Segment_Controller _7_SEGMENT_CONTROLLER (.BCD(binarytobcd_1_bcd9), .out_2(_7_Segment_9));
  _7_Segment_Controller u_7_segment_controller_1 (.BCD(binarytobcd_1_bcd8), .out_2(_7_Segment_8));
  _7_Segment_Controller u_7_segment_controller_2 (.BCD(binarytobcd_1_bcd7), .out_2(_7_Segment_7));
  _7_Segment_Controller u_7_segment_controller_3 (.BCD(binarytobcd_1_bcd6), .out_2(_7_Segment_6));
  _7_Segment_Controller u_7_segment_controller_4 (.BCD(binarytobcd_1_bcd5), .out_2(_7_Segment_5));
  _7_Segment_Controller u_7_segment_controller_5 (.BCD(binarytobcd_1_bcd4), .out_2(_7_Segment_4));
  _7_Segment_Controller u_7_segment_controller_6 (.BCD(binarytobcd_1_bcd3), .out_2(_7_Segment_3));
  _7_Segment_Controller u_7_segment_controller_7 (.BCD(binarytobcd_1_bcd2), .out_2(_7_Segment_2));
  _7_Segment_Controller u_7_segment_controller_8 (.BCD(binarytobcd_1_bcd1), .out_2(_7_Segment_1));
  _7_Segment_Controller u_7_segment_controller_9 (.BCD(binarytobcd_1_bcd0), .out_2(_7_Segment_0));

  assign Minus[6:1] = {6{1'b0}};
endmodule

module _7_Segment_Controller (
  input  [3:0] BCD,
  output [6:0] out_2
);

  wire and_1_out, and_2_out, and_3_out, and_4_out, and_5_out, and_6_out, and_7_out, and_8_out, and_9_out,
       and_10_out, and_11_out, and_12_out, and_13_out, and_14_out, and_15_out, and_16_out, not_1_out,
       not_2_out, not_3_out, not_4_out, not_5_out, not_6_out, not_7_out, not_8_out, not_9_out, not_10_out,
       not_11_out, not_12_out, not_13_out, not_14_out, not_15_out, not_16_out, not_17_out, not_18_out,
       not_19_out, not_20_out, not_21_out;

  not not_1 (not_1_out, BCD[2]);
  not not_2 (not_2_out, BCD[0]);
  not not_3 (not_3_out, BCD[1]);
  not not_4 (not_4_out, BCD[1]);
  not not_5 (not_5_out, BCD[0]);
  not not_6 (not_6_out, BCD[1]);
  not not_7 (not_7_out, BCD[0]);
  not not_8 (not_8_out, BCD[2]);
  not not_9 (not_9_out, BCD[0]);
  not not_10 (not_10_out, BCD[1]);
  not not_11 (not_11_out, BCD[0]);
  not not_12 (not_12_out, BCD[2]);
  not not_13 (not_13_out, BCD[0]);
  not not_14 (not_14_out, BCD[0]);
  not not_15 (not_15_out, BCD[2]);
  not not_16 (not_16_out, BCD[0]);
  not not_17 (not_17_out, BCD[2]);
  not not_18 (not_18_out, BCD[0]);
  not not_19 (not_19_out, BCD[1]);
  not not_20 (not_20_out, BCD[1]);
  and and_1 (and_1_out, not_1_out, BCD[1]);
  and and_2 (and_2_out, BCD[1], not_2_out);
  and and_3 (and_3_out, BCD[2], not_3_out);
  and and_4 (and_4_out, not_4_out, not_5_out);
  and and_5 (and_5_out, BCD[2], not_6_out);
  and and_6 (and_6_out, BCD[2], not_7_out);
  and and_7 (and_7_out, not_8_out, not_9_out);
  and and_8 (and_8_out, BCD[2], BCD[0]);
  not not_21 (not_21_out, BCD[2]);
  and and_9 (and_9_out, not_10_out, not_11_out);
  and and_10 (and_10_out, BCD[1], BCD[0]);
  and and_11 (and_11_out, not_12_out, not_13_out);
  and and_12 (and_12_out, BCD[1], not_14_out);
  and and_13 (and_13_out, not_15_out, not_16_out);
  and and_14 (and_14_out, not_17_out, BCD[1]);
  and and_15 (and_15_out, BCD[1], not_18_out);
  and and_16 (and_16_out, BCD[2], not_19_out, BCD[0]);
  or or_1 (out_2[6], not_20_out, BCD[0], BCD[2]);
  or or_2 (out_2[0], and_1_out, and_2_out, and_3_out, BCD[3]);
  or or_3 (out_2[1], and_4_out, and_5_out, and_6_out, BCD[3]);
  or or_4 (out_2[2], and_7_out, BCD[1], and_8_out, BCD[3]);
  or or_5 (out_2[3], not_21_out, and_9_out, and_10_out);
  or or_6 (out_2[4], and_11_out, and_12_out);
  or or_7 (out_2[5], and_13_out, and_14_out, and_15_out, and_16_out);
endmodule

module BinaryToBCD (
  input  [31:0] Input,
  output Minus,
  output [3:0] BCD9,
  output [3:0] BCD8,
  output [3:0] BCD7,
  output [3:0] BCD6,
  output [3:0] BCD5,
  output [3:0] BCD4,
  output [3:0] BCD3,
  output [3:0] BCD2,
  output [3:0] BCD1,
  output [3:0] BCD0
);

  wire [27:0] subtractor_1_out, subtractor_2_out, subtractor_3_out, subtractor_4_out, subtractor_5_out,
       subtractor_6_out, subtractor_7_out, subtractor_8_out, subtractor_9_out;
  wire [31:0] adder_1_out, divider_1_out, divider_2_out, divider_3_out, divider_4_out, divider_5_out,
       divider_6_out, divider_7_out, divider_8_out, multiplexer_1_out, multiplier_1_out, multiplier_2_out,
       multiplier_3_out, multiplier_4_out, multiplier_5_out, multiplier_6_out, multiplier_7_out,
       multiplier_8_out, multiplier_9_out, not_1_out;
  wire [31:4] divider_9_out;

  assign not_1_out = ~Input;  // NOT_Gate not_1, 32 bits wide
  Adder #(.width(32)) adder_1 (.a(not_1_out), .b(32'h1), .out(adder_1_out));  // open: cin, cout
  Multiplexer #(.width(32)) multiplexer_1 (
    .in0(Input), .in1(adder_1_out), .out(multiplexer_1_out), .sel(Input[31]));  // open: en
  Subtractor #(.width(32)) subtractor_1 (
    .a(multiplexer_1_out), .b(multiplier_1_out), .out({subtractor_1_out, BCD0}));  // open: bin, bout
  Multiplier #(.width(32)) multiplier_1 (.a(divider_1_out), .b(32'ha), .out(multiplier_1_out));  // open: cin, cout
  Divider #(.width(32)) divider_1 (.a(multiplexer_1_out), .b(32'ha), .out(divider_1_out));  // open: upper, rem
  Subtractor #(.width(32)) subtractor_2 (
    .a(divider_1_out), .b(multiplier_2_out), .out({subtractor_2_out, BCD1}));  // open: bin, bout
  Multiplier #(.width(32)) multiplier_2 (.a(divider_2_out), .b(32'ha), .out(multiplier_2_out));  // open: cin, cout
  Divider #(.width(32)) divider_2 (.a(divider_1_out), .b(32'ha), .out(divider_2_out));  // open: upper, rem
  Subtractor #(.width(32)) subtractor_3 (
    .a(divider_2_out), .b(multiplier_3_out), .out({subtractor_3_out, BCD2}));  // open: bin, bout
  Multiplier #(.width(32)) multiplier_3 (.a(divider_3_out), .b(32'ha), .out(multiplier_3_out));  // open: cin, cout
  Divider #(.width(32)) divider_3 (.a(divider_2_out), .b(32'ha), .out(divider_3_out));  // open: upper, rem
  Subtractor #(.width(32)) subtractor_4 (
    .a(divider_3_out), .b(multiplier_4_out), .out({subtractor_4_out, BCD3}));  // open: bin, bout
  Multiplier #(.width(32)) multiplier_4 (.a(divider_4_out), .b(32'ha), .out(multiplier_4_out));  // open: cin, cout
  Divider #(.width(32)) divider_4 (.a(divider_3_out), .b(32'ha), .out(divider_4_out));  // open: upper, rem
  Subtractor #(.width(32)) subtractor_5 (
    .a(divider_4_out), .b(multiplier_5_out), .out({subtractor_5_out, BCD4}));  // open: bin, bout
  Multiplier #(.width(32)) multiplier_5 (.a(divider_5_out), .b(32'ha), .out(multiplier_5_out));  // open: cin, cout
  Divider #(.width(32)) divider_5 (.a(divider_4_out), .b(32'ha), .out(divider_5_out));  // open: upper, rem
  Subtractor #(.width(32)) subtractor_6 (
    .a(divider_5_out), .b(multiplier_6_out), .out({subtractor_6_out, BCD5}));  // open: bin, bout
  Multiplier #(.width(32)) multiplier_6 (.a(divider_6_out), .b(32'ha), .out(multiplier_6_out));  // open: cin, cout
  Divider #(.width(32)) divider_6 (.a(divider_5_out), .b(32'ha), .out(divider_6_out));  // open: upper, rem
  Subtractor #(.width(32)) subtractor_7 (
    .a(divider_6_out), .b(multiplier_7_out), .out({subtractor_7_out, BCD6}));  // open: bin, bout
  Multiplier #(.width(32)) multiplier_7 (.a(divider_7_out), .b(32'ha), .out(multiplier_7_out));  // open: cin, cout
  Divider #(.width(32)) divider_7 (.a(divider_6_out), .b(32'ha), .out(divider_7_out));  // open: upper, rem
  Subtractor #(.width(32)) subtractor_8 (
    .a(divider_7_out), .b(multiplier_8_out), .out({subtractor_8_out, BCD7}));  // open: bin, bout
  Multiplier #(.width(32)) multiplier_8 (.a(divider_8_out), .b(32'ha), .out(multiplier_8_out));  // open: cin, cout
  Divider #(.width(32)) divider_8 (.a(divider_7_out), .b(32'ha), .out(divider_8_out));  // open: upper, rem
  Subtractor #(.width(32)) subtractor_9 (
    .a(divider_8_out), .b(multiplier_9_out), .out({subtractor_9_out, BCD8}));  // open: bin, bout
  Multiplier #(.width(32)) multiplier_9 (
    .a({divider_9_out, BCD9}), .b(32'ha), .out(multiplier_9_out));  // open: cin, cout
  Divider #(.width(32)) divider_9 (.a(divider_8_out), .b(32'ha), .out({divider_9_out, BCD9}));  // open: upper, rem

  assign Minus = Input[31];
endmodule

module Keypad_Controller (
  input  C,
  input  in_2,
  input  in_3,
  input  in_4,
  input  in_5,
  input  in_6,
  input  _9,
  input  _8,
  input  _7,
  input  _6,
  input  _5,
  input  _4,
  input  _3,
  input  _2,
  input  _1,
  input  _0,
  input  [31:0] From__t9,
  output Write,
  output [31:0] Output
);

  wire ISZERO_2_out_2, ISZERO_out_2;
  wire [3:0] or_4_out;
  wire [15:0] and_1_out;

  and and_1 (and_1_out[0], C, ISZERO_out_2);
  and and_2 (and_1_out[1], in_2, ISZERO_out_2);
  and and_3 (and_1_out[2], in_3, ISZERO_out_2);
  and and_4 (and_1_out[3], in_4, ISZERO_out_2);
  and and_5 (and_1_out[4], in_5, ISZERO_out_2);
  and and_6 (and_1_out[5], in_6, ISZERO_out_2);
  and and_7 (and_1_out[6], _9, ISZERO_out_2);
  and and_8 (and_1_out[7], _8, ISZERO_out_2);
  and and_9 (and_1_out[8], _7, ISZERO_out_2);
  and and_10 (and_1_out[9], _6, ISZERO_out_2);
  and and_11 (and_1_out[10], _5, ISZERO_out_2);
  and and_12 (and_1_out[11], _4, ISZERO_out_2);
  and and_13 (and_1_out[12], _3, ISZERO_out_2);
  and and_14 (and_1_out[13], _2, ISZERO_out_2);
  and and_15 (and_1_out[14], _1, ISZERO_out_2);
  and and_16 (and_1_out[15], _0, ISZERO_out_2);
  isZero ISZERO (.Input(From__t9), .out_2(ISZERO_out_2));
  or or_1 (or_4_out[3], and_1_out[0], and_1_out[1], and_1_out[2], and_1_out[3], and_1_out[4], and_1_out[5], and_1_out[6], and_1_out[7]);
  or or_2 (or_4_out[2], and_1_out[8], and_1_out[9], and_1_out[10], and_1_out[11], and_1_out[0], and_1_out[1], and_1_out[2], and_1_out[3]);
  or or_3 (or_4_out[1], and_1_out[12], and_1_out[13], and_1_out[9], and_1_out[8], and_1_out[5], and_1_out[4], and_1_out[1], and_1_out[0]);
  or or_4 (or_4_out[0], and_1_out[12], and_1_out[14], and_1_out[10], and_1_out[8], and_1_out[6], and_1_out[4], and_1_out[2], and_1_out[0]);
  isZero ISZERO_2 (.Input({{16{1'b0}}, and_1_out}), .out_2(ISZERO_2_out_2));
  not not_1 (Write, ISZERO_2_out_2);
  assign Output = Write ? {28'h8000000, or_4_out} : 32'bz;  // Controlled_Buffer controlled_buffer_1
endmodule

module isZero (
  input  [31:0] Input,
  output out_2
);

  wire or_1_out;

  or or_1 (or_1_out, Input[0], Input[1], Input[2], Input[3], Input[4], Input[5], Input[6], Input[7], Input[8], Input[9], Input[10], Input[11], Input[12], Input[13], Input[14], Input[15], Input[16], Input[17], Input[18], Input[19], Input[20], Input[21], Input[22], Input[23], Input[24], Input[25], Input[26], Input[27], Input[28], Input[29], Input[30], Input[31]);
  not not_1 (out_2, or_1_out);
endmodule

module Instruction_Memory__FINISHED (
  input  [15:0] Input,
  output [31:0] out_2
);

  ROM #(.addrWidth(16), .dataWidth(32)) rom_1 (.addr(Input), .data(out_2), .sel(1'b1));

  // Notes on the sheet:
  //   contents of rom_1 (hex, n*v repeats v):
  //   1320ffff 198020 3210000f 2001000f 1030009a 2001ffff 14300001 8100000 2001000a 10300014 2001000b
  //   10300012 2001000c 10300010 2001000d 1030000e 214a0001 20010001 142a0004 106820 dc020 c820 8100000
  //   d4040 d48c0 1096020 1906820 dc020 c820 8100000 109820 c820 8100021 1320ffff 199020 3252000f 2001000a
  //   10320023 2001000b 10320021 2001000c 1032001f 2001000d 1032001d 2001000f 10320071 2001000e 10320019
  //   2001ffff 14320001 8100021 20150001 5020 4020 4820 6020 216b0001 20010001 142b0007 127020 ec020 c820
  //   8100021 129820 c820 8100021 e4040 e48c0 1096020 1927020 ec020 c820 8100021 20010001 1435fff4 12b820
  //   2001000a 10330011 2001000b 10330014 2001000c 10330017 2001000d 1033002c a820 2001000e 10370045 f6820
  //   179820 b820 5820 8100021 f6820 c820 8100000 1aea820 157820 fc020 c820 8100054 1aea822 157820 fc020
  //   c820 8100054 1e0802a 20010001 1030000a 6020 b020 12cd0003 18e6020 22d60001 810006e c7820 fc020 c820
  //   8100054 6020 b020 12cd0003 18e6020 22d6ffff 8100078 c7822 fc020 c820 8100054 1a0802a 20010001
  //   1030000c 6020 1ae802a 20010001 10300004 1ae6822 dc020 218c0001 8100084 c7820 fc020 c820 8100054
  //   d6822 6020 1ae802a 20010001 10300004 1ae6822 dc020 218c0001 8100091 c7822 fc020 c820 8100054 fc020
  //   5820 810005c c020 4020 4820 5020 5820 6020 6820 7020 7820 c820 8020 8820 9020 9820 a020 a820 b020
  //   b820 8100000
endmodule

module Shift_Left__FINISHED (
  input  [31:0] Input,
  input  [4:0] shift_amt,
  output [31:0] \output 
);

  Shifter #(.width(32)) shifter_1 (.in(Input), .\dist (shift_amt), .out(\output ));
endmodule

module Shift_Right__FINISHED (
  input  [31:0] Input,
  input  [4:0] shift_amt,
  output [31:0] \output 
);

  Shifter #(.width(32), .shift("lr")) shifter_1 (.in(Input), .\dist (shift_amt), .out(\output ));
endmodule

module Sign_Extend__FINISHED (
  input  [15:0] Input,
  output [31:0] Extended
);


  assign Extended = {{17{Input[15]}}, Input[14:0]};
endmodule

module CPU (
  input  [31:0] Write_to__t9,
  input  Write_To_Keyboard,
  output [31:0] from_t8,
  output [31:0] from_t9
);

  wire and_1_out, and_2_out, clock_1_out, control_unit_finished_1_addi, control_unit_finished_1_alu_source,
       control_unit_finished_1_beq, control_unit_finished_1_bne, control_unit_finished_1_jump,
       control_unit_finished_1_register_destination, control_unit_finished_1_register_write,
       n32_bit_alu_finished_1_zero, not_1_out, or_1_out;
  wire [1:0] alu_control_1_shift, control_unit_finished_1_alu_opcode;
  wire [3:0] alu_control_1_out_3, multiplexer_3_out;
  wire [4:0] instruction_memory_finished_1_out_2_2, multiplexer_1_out;
  wire [25:0] shifter_1_out;
  wire [31:0] adder_1_out, adder_2_out, instruction_memory_finished_1_out_2, multiplexer_2_out,
       multiplexer_4_out, multiplexer_5_out, n32_bit_alu_finished_1_result, register_1_q,
       register_file_finished_1_read_data_1, register_file_finished_1_read_data_2, shifter_2_out,
       sign_extend_finished_1_extended;

  Clock clock_1 (.out(clock_1_out));
  Register #(.width(32)) register_1 (.D(multiplexer_5_out), .Q(register_1_q), .clk(clock_1_out));  // open: en, clr
  Adder #(.width(32)) adder_1 (.a(register_1_q), .b(32'h4), .out(adder_1_out));  // open: cin, cout
  Instruction_Memory__FINISHED instruction_memory_finished_1 (
    .Input(register_1_q[17:2]),
    .out_2({instruction_memory_finished_1_out_2[31:11], instruction_memory_finished_1_out_2_2, instruction_memory_finished_1_out_2[5:0]}));
  Shifter #(.width(26)) shifter_1 (
    .in({instruction_memory_finished_1_out_2[25:11], instruction_memory_finished_1_out_2_2, instruction_memory_finished_1_out_2[5:0]}),
    .\dist (5'b00010), .out(shifter_1_out));
  Control_unit_FINISHED control_unit_finished_1 (
    .opcode(instruction_memory_finished_1_out_2[31:26]), .jump(control_unit_finished_1_jump),
    .register_destination(control_unit_finished_1_register_destination),
    .register_write(control_unit_finished_1_register_write), .ALU_source(control_unit_finished_1_alu_source),
    .beq(control_unit_finished_1_beq), .ALU_opcode(control_unit_finished_1_alu_opcode),
    .bne(control_unit_finished_1_bne), .addi(control_unit_finished_1_addi));
  Multiplexer #(.width(5)) multiplexer_1 (
    .in0(instruction_memory_finished_1_out_2[20:16]), .in1(instruction_memory_finished_1_out_2[15:11]),
    .out(multiplexer_1_out), .sel(control_unit_finished_1_register_destination));  // open: en
  Sign_Extend__FINISHED sign_extend_finished_1 (
    .Input({instruction_memory_finished_1_out_2[15:11], instruction_memory_finished_1_out_2_2, instruction_memory_finished_1_out_2[5:0]}),
    .Extended(sign_extend_finished_1_extended));
  Register_File_FINISHED register_file_finished_1 (
    .write_data(n32_bit_alu_finished_1_result), .Write_Register(multiplexer_1_out),
    .read_register_1(instruction_memory_finished_1_out_2[25:21]),
    .read_register_2(instruction_memory_finished_1_out_2[20:16]), .write_to_t9(Write_to__t9),
    .keypad(Write_To_Keyboard), .Write_signal(control_unit_finished_1_register_write), .clock(clock_1_out),
    .read_data_1(register_file_finished_1_read_data_1), .read_data_2(register_file_finished_1_read_data_2),
    .from_t8(from_t8), .from_t9(from_t9));
  Shifter #(.width(32)) shifter_2 (.in(sign_extend_finished_1_extended), .\dist (5'b00010), .out(shifter_2_out));
  ALU_control alu_control_1 (
    .Input(instruction_memory_finished_1_out_2[5:0]), .alu_op(control_unit_finished_1_alu_opcode),
    .out_3(alu_control_1_out_3), .shift(alu_control_1_shift));
  Adder #(.width(32)) adder_2 (.a(adder_1_out), .b(shifter_2_out), .out(adder_2_out));  // open: cin, cout
  not not_1 (not_1_out, n32_bit_alu_finished_1_zero);
  Multiplexer #(.width(32)) multiplexer_2 (
    .in0(register_file_finished_1_read_data_2), .in1(sign_extend_finished_1_extended),
    .out(multiplexer_2_out), .sel(control_unit_finished_1_alu_source));  // open: en
  Multiplexer #(.width(4)) multiplexer_3 (
    .in0(alu_control_1_out_3), .in1(4'b0010), .out(multiplexer_3_out), .sel(control_unit_finished_1_addi));  // open: en
  and and_1 (and_1_out, control_unit_finished_1_bne, not_1_out);
  and and_2 (and_2_out, control_unit_finished_1_beq, n32_bit_alu_finished_1_zero);
  _32_bit_ALU_FINISHED u_32_bit_alu_finished_1 (
    .a(register_file_finished_1_read_data_1), .b(multiplexer_2_out),
    .shamt(instruction_memory_finished_1_out_2_2), .Ainvert(multiplexer_3_out[3]),
    .Binvert(multiplexer_3_out[2]), .Operation(multiplexer_3_out[1:0]),
    .Shift_Operation(alu_control_1_shift), .Zero(n32_bit_alu_finished_1_zero),
    .Result(n32_bit_alu_finished_1_result));  // open: Less, CarryIn, CarryOut, Set
  Multiplexer #(.width(32), .enable("false")) multiplexer_4 (
    .in0(adder_1_out), .in1(adder_2_out), .out(multiplexer_4_out), .sel(or_1_out));
  or or_1 (or_1_out, and_1_out, and_2_out);
  Multiplexer #(.width(32), .enable("false")) multiplexer_5 (
    .in0(multiplexer_4_out), .in1({adder_1_out[31:26], shifter_1_out}), .out(multiplexer_5_out),
    .sel(control_unit_finished_1_jump));
endmodule

module ALU_control (
  input  [5:0] Input,
  input  [1:0] alu_op,
  output [3:0] out_3,
  output [1:0] shift
);

  wire not_1_out, not_2_out, not_3_out, not_4_out, not_5_out, not_6_out, not_7_out, not_8_out, not_9_out,
       not_10_out, not_11_out, not_12_out;
  wire [0:0] and_1_out;
  wire [1:1] and_2_out;
  wire [2:0] or_1_out;

  not not_1 (not_1_out, Input[5]);
  not not_2 (not_2_out, Input[1]);
  not not_3 (not_3_out, Input[0]);
  not not_4 (not_4_out, Input[4]);
  not not_5 (not_5_out, Input[3]);
  not not_6 (not_6_out, Input[2]);
  and and_1 (and_1_out[0], not_1_out, not_4_out, not_3_out, not_2_out, not_6_out, not_5_out);
  not not_7 (not_7_out, Input[2]);
  not not_8 (not_8_out, Input[0]);
  not not_9 (not_9_out, Input[2]);
  not not_10 (not_10_out, Input[4]);
  not not_11 (not_11_out, Input[5]);
  not not_12 (not_12_out, Input[3]);
  and and_2 (and_2_out[1], not_9_out, not_12_out, not_8_out, not_10_out, not_11_out, Input[1]);
  and and_3 (or_1_out[1], not_7_out, Input[5]);
  and and_4 (or_1_out[2], Input[1], Input[5]);
  or or_1 (or_1_out[0], Input[0], Input[3]);
  assign shift = {1'b0, and_1_out[0]} | {and_2_out[1], 1'b0};  // OR_Gate or_2, 2 bits wide
  Multiplexer #(.select(2), .width(4)) multiplexer_1 (
    .in0(4'b0010), .in1(4'b0110), .in2({1'b0, or_1_out}), .in3(4'b0111), .out(out_3), .sel(alu_op));  // open: en
endmodule

module Control_unit_FINISHED (
  input  [5:0] opcode,
  output jump,
  output register_destination,
  output register_write,
  output ALU_source,
  output beq,
  output [1:0] ALU_opcode,
  output bne,
  output addi
);

  wire and_3_out, and_9_out, not_1_out, not_2_out, not_3_out, not_4_out, not_5_out, not_6_out, not_7_out,
       not_8_out, not_9_out, not_10_out, not_11_out, not_12_out, not_13_out, not_14_out, not_15_out,
       not_16_out, not_17_out, not_18_out, not_19_out, not_20_out, not_21_out, not_22_out, not_23_out,
       not_24_out, not_25_out, not_26_out, not_27_out, not_28_out, not_29_out, not_30_out, not_31_out,
       not_32_out, not_33_out, not_34_out, not_35_out, not_36_out, not_37_out, or_1_out;

  not not_1 (not_1_out, opcode[1]);
  and and_1 (addi, not_1_out, not_4_out, not_5_out, not_2_out, not_3_out, opcode[3]);
  not not_2 (not_2_out, opcode[0]);
  not not_3 (not_3_out, opcode[2]);
  and and_2 (jump, opcode[1], not_3_out, not_2_out, not_6_out, not_5_out, not_4_out);
  not not_4 (not_4_out, opcode[5]);
  and and_3 (and_3_out, opcode[1], opcode[3]);
  not not_5 (not_5_out, opcode[4]);
  not not_6 (not_6_out, opcode[3]);
  not not_7 (not_7_out, opcode[1]);
  not not_8 (not_8_out, opcode[4]);
  not not_9 (not_9_out, opcode[0]);
  not not_10 (not_10_out, opcode[5]);
  not not_11 (not_11_out, opcode[3]);
  and and_4 (beq, not_9_out, not_8_out, not_7_out, not_10_out, opcode[2], not_11_out);
  not not_12 (not_12_out, opcode[0]);
  not not_13 (not_13_out, opcode[3]);
  not not_14 (not_14_out, opcode[3]);
  not not_15 (not_15_out, opcode[4]);
  not not_16 (not_16_out, opcode[2]);
  // AND_Gate and_5 has open pins: in0=not_12_out, in1=opcode[1], in2=opcode[5], in3=not_16_out, in4=not_14_out, in5=not_15_out, out=open
  or or_1 (or_1_out, beq, bne);
  not not_17 (not_17_out, opcode[5]);
  not not_18 (not_18_out, opcode[1]);
  not not_19 (not_19_out, opcode[3]);
  and and_6 (bne, opcode[0], not_18_out, opcode[2], not_19_out, not_20_out, not_21_out);
  not not_20 (not_20_out, opcode[4]);
  not not_21 (not_21_out, opcode[5]);
  or or_2 (ALU_opcode[0], or_1_out, and_3_out);
  not not_22 (not_22_out, opcode[2]);
  not not_23 (not_23_out, opcode[4]);
  not not_24 (not_24_out, opcode[3]);
  // AND_Gate and_7 has open pins: in0=not_22_out, in1=not_24_out, in2=not_23_out, in3=opcode[1], in4=opcode[0], in5=opcode[5], out=open
  not not_25 (not_25_out, or_1_out);
  not not_26 (not_26_out, jump);
  not not_27 (not_27_out, opcode[0]);
  not not_28 (not_28_out, opcode[2]);
  not not_29 (not_29_out, opcode[1]);
  not not_30 (not_30_out, beq);
  not not_31 (not_31_out, jump);
  not not_32 (not_32_out, beq);
  not not_33 (not_33_out, bne);
  and and_8 (ALU_opcode[1], not_25_out, not_26_out);
  not not_34 (not_34_out, opcode[5]);
  not not_35 (not_35_out, opcode[3]);
  not not_36 (not_36_out, opcode[4]);
  and and_9 (and_9_out, not_27_out, not_29_out, not_28_out, not_35_out, not_36_out, not_34_out);
  and and_10 (register_destination, not_17_out, not_13_out);
  not not_37 (not_37_out, and_9_out);
  and and_11 (register_write, not_30_out, not_31_out, not_33_out);
  and and_12 (ALU_source, not_37_out, not_32_out, not_33_out);
endmodule

module _32_bit_ALU_FINISHED (
  input  Ainvert,
  input  CarryIn,
  input  Binvert,
  input  [1:0] Operation,
  input  [31:0] a,
  input  [31:0] b,
  input  [31:0] Less,
  input  [4:0] shamt,
  input  [1:0] Shift_Operation,
  output Zero,
  output CarryOut,
  output [31:0] Set,
  output [31:0] Result
);

  wire [31:0] and_1_out, multiplexer_1_out, multiplexer_2_out, multiplexer_3_out, not_1_out, not_2_out,
       or_1_out, shift_left_finished_1_output, shift_right_finished_1_output;

  assign not_1_out = ~a;  // NOT_Gate not_1, 32 bits wide
  Multiplexer #(.width(32), .enable("false")) multiplexer_1 (
    .in0(a), .in1(not_1_out), .out(multiplexer_1_out), .sel(Ainvert));
  assign not_2_out = ~b;  // NOT_Gate not_2, 32 bits wide
  Multiplexer #(.width(32), .enable("false")) multiplexer_2 (
    .in0(b), .in1(not_2_out), .out(multiplexer_2_out), .sel(Binvert));
  Shift_Left__FINISHED shift_left_finished_1 (.Input(b), .shift_amt(shamt), .\output (shift_left_finished_1_output));
  Shift_Right__FINISHED shift_right_finished_1 (.Input(b), .shift_amt(shamt), .\output (shift_right_finished_1_output));
  assign and_1_out = multiplexer_1_out & multiplexer_2_out;  // AND_Gate and_1, 32 bits wide
  assign or_1_out = multiplexer_1_out | multiplexer_2_out;  // OR_Gate or_1, 32 bits wide
  Adder #(.width(32)) adder_1 (.a(multiplexer_1_out), .b(multiplexer_2_out), .out(Set), .cin(CarryIn), .cout(CarryOut));
  Multiplexer #(.select(2), .width(32), .enable("false")) multiplexer_3 (
    .in0(and_1_out), .in1(or_1_out), .in2(Set), .in3(Less), .out(multiplexer_3_out), .sel(Operation));
  isZero iszero_1 (.Input(multiplexer_3_out), .out_2(Zero));
  Multiplexer #(.select(2), .width(32)) multiplexer_4 (
    .in0(multiplexer_3_out), .in2(shift_left_finished_1_output), .in3(shift_right_finished_1_output),
    .out(Result), .sel(Shift_Operation));  // open: in1, en
endmodule

module Register_File_FINISHED (
  input  Write_signal,
  input  [31:0] write_data,
  input  [4:0] Write_Register,
  input  [4:0] read_register_1,
  input  [4:0] read_register_2,
  input  [31:0] write_to_t9,
  input  keypad,
  input  clock,
  output [31:0] read_data_1,
  output [31:0] read_data_2,
  output [31:0] from_t8,
  output [31:0] from_t9
);

  wire _0_out, _1_out, _2_out, _3_out, _4_out, _5_out, _6_out, _7_out, _8_out, _9_out, _10_out, _11_out,
       _12_out, _13_out, _14_out, _15_out, _16_out, _17_out, _18_out, _19_out, _20_out, _21_out, _22_out,
       _23_out, _24_out, _25_out, _26_out, _27_out, _28_out, _29_out, _30_out, _31_out,
       controlled_buffer_2_out, decoder_1_out0, decoder_1_out1, decoder_1_out2, decoder_1_out3,
       decoder_1_out4, decoder_1_out5, decoder_1_out6, decoder_1_out7, decoder_1_out8, decoder_1_out9,
       decoder_1_out10, decoder_1_out11, decoder_1_out12, decoder_1_out13, decoder_1_out14, decoder_1_out15,
       decoder_1_out16, decoder_1_out17, decoder_1_out18, decoder_1_out19, decoder_1_out20, decoder_1_out21,
       decoder_1_out22, decoder_1_out23, decoder_1_out24, decoder_1_out25, decoder_1_out26, decoder_1_out27,
       decoder_1_out28, decoder_1_out29, decoder_1_out30, decoder_1_out31;
  wire [31:0] _26_2_q, _27_2_q, _28_2_q, _29_2_q, _30_2_q, _31_2_q, controlled_buffer_1_out, register_1_q,
       register_2_q, register_3_q, register_4_q, register_5_q, register_6_q, register_7_q, register_8_q,
       register_9_q, register_10_q, register_11_q, register_12_q, register_13_q, register_14_q,
       register_15_q, register_16_q, register_17_q, register_18_q, register_19_q, register_20_q,
       register_21_q, register_22_q, register_23_q, register_24_q;

  Decoder #(.select(5)) decoder_1 (
    .out0(decoder_1_out0), .out1(decoder_1_out1), .out2(decoder_1_out2), .out3(decoder_1_out3),
    .out4(decoder_1_out4), .out5(decoder_1_out5), .out6(decoder_1_out6), .out7(decoder_1_out7),
    .out8(decoder_1_out8), .out9(decoder_1_out9), .out10(decoder_1_out10), .out11(decoder_1_out11),
    .out12(decoder_1_out12), .out13(decoder_1_out13), .out14(decoder_1_out14), .out15(decoder_1_out15),
    .out16(decoder_1_out16), .out17(decoder_1_out17), .out18(decoder_1_out18), .out19(decoder_1_out19),
    .out20(decoder_1_out20), .out21(decoder_1_out21), .out22(decoder_1_out22), .out23(decoder_1_out23),
    .out24(decoder_1_out24), .out25(decoder_1_out25), .out26(decoder_1_out26), .out27(decoder_1_out27),
    .out28(decoder_1_out28), .out29(decoder_1_out29), .out30(decoder_1_out30), .out31(decoder_1_out31),
    .sel(Write_Register));  // open: en
  assign controlled_buffer_1_out = keypad ? write_to_t9 : 32'bz;  // Controlled_Buffer controlled_buffer_1
  assign controlled_buffer_2_out = keypad ? keypad : 1'bz;  // Controlled_Buffer controlled_buffer_2
  and _0 (_0_out, Write_signal, decoder_1_out0);
  and _1 (_1_out, Write_signal, decoder_1_out1);
  and _2 (_2_out, Write_signal, decoder_1_out2);
  and _3 (_3_out, Write_signal, decoder_1_out3);
  and _4 (_4_out, Write_signal, decoder_1_out4);
  and _5 (_5_out, Write_signal, decoder_1_out5);
  and _6 (_6_out, Write_signal, decoder_1_out6);
  and _7 (_7_out, Write_signal, decoder_1_out7);
  and _8 (_8_out, Write_signal, decoder_1_out8);
  and _9 (_9_out, Write_signal, decoder_1_out9);
  and _10 (_10_out, Write_signal, decoder_1_out10);
  and _11 (_11_out, Write_signal, decoder_1_out11);
  and _12 (_12_out, Write_signal, decoder_1_out12);
  and _13 (_13_out, Write_signal, decoder_1_out13);
  and _14 (_14_out, Write_signal, decoder_1_out14);
  and _15 (_15_out, Write_signal, decoder_1_out15);
  and _16 (_16_out, Write_signal, decoder_1_out16);
  and _17 (_17_out, Write_signal, decoder_1_out17);
  and _18 (_18_out, Write_signal, decoder_1_out18);
  and _19 (_19_out, Write_signal, decoder_1_out19);
  and _20 (_20_out, Write_signal, decoder_1_out20);
  and _21 (_21_out, Write_signal, decoder_1_out21);
  and _22 (_22_out, Write_signal, decoder_1_out22);
  and _23 (_23_out, Write_signal, decoder_1_out23);
  and _24 (_24_out, Write_signal, decoder_1_out24);
  and _25 (_25_out, Write_signal, decoder_1_out25);
  assign controlled_buffer_1_out = _25_out ? write_data : 32'bz;  // Controlled_Buffer controlled_buffer_3
  and _26 (_26_out, Write_signal, decoder_1_out26);
  assign controlled_buffer_2_out = _25_out ? _25_out : 1'bz;  // Controlled_Buffer controlled_buffer_4
  and _27 (_27_out, Write_signal, decoder_1_out27);
  and _28 (_28_out, Write_signal, decoder_1_out28);
  and _29 (_29_out, Write_signal, decoder_1_out29);
  and _30 (_30_out, Write_signal, decoder_1_out30);
  and _31 (_31_out, Write_signal, decoder_1_out31);
  Register #(.width(32)) register_1 (.D(write_data), .en(_0_out), .Q(register_1_q), .clk(clock));  // open: clr
  Register #(.width(32)) register_2 (.D(write_data), .en(_1_out), .Q(register_2_q), .clk(clock));  // open: clr
  Register #(.width(32)) register_3 (.D(write_data), .en(_2_out), .Q(register_3_q), .clk(clock));  // open: clr
  Register #(.width(32)) register_4 (.D(write_data), .en(_3_out), .Q(register_4_q), .clk(clock));  // open: clr
  Register #(.width(32)) register_5 (.D(write_data), .en(_4_out), .Q(register_5_q), .clk(clock));  // open: clr
  Register #(.width(32)) register_6 (.D(write_data), .en(_5_out), .Q(register_6_q), .clk(clock));  // open: clr
  Register #(.width(32)) register_7 (.D(write_data), .en(_6_out), .Q(register_7_q), .clk(clock));  // open: clr
  Register #(.width(32)) register_8 (.D(write_data), .en(_7_out), .Q(register_8_q), .clk(clock));  // open: clr
  Register #(.width(32)) register_9 (.D(write_data), .en(_8_out), .Q(register_9_q), .clk(clock));  // open: clr
  Register #(.width(32)) register_10 (.D(write_data), .en(_9_out), .Q(register_10_q), .clk(clock));  // open: clr
  Register #(.width(32)) register_11 (.D(write_data), .en(_10_out), .Q(register_11_q), .clk(clock));  // open: clr
  Register #(.width(32)) register_12 (.D(write_data), .en(_11_out), .Q(register_12_q), .clk(clock));  // open: clr
  Register #(.width(32)) register_13 (.D(write_data), .en(_12_out), .Q(register_13_q), .clk(clock));  // open: clr
  Register #(.width(32)) register_14 (.D(write_data), .en(_13_out), .Q(register_14_q), .clk(clock));  // open: clr
  Register #(.width(32)) register_15 (.D(write_data), .en(_14_out), .Q(register_15_q), .clk(clock));  // open: clr
  Register #(.width(32)) register_16 (.D(write_data), .en(_15_out), .Q(register_16_q), .clk(clock));  // open: clr
  Register #(.width(32)) register_17 (.D(write_data), .en(_16_out), .Q(register_17_q), .clk(clock));  // open: clr
  Register #(.width(32)) register_18 (.D(write_data), .en(_17_out), .Q(register_18_q), .clk(clock));  // open: clr
  Register #(.width(32)) register_19 (.D(write_data), .en(_18_out), .Q(register_19_q), .clk(clock));  // open: clr
  Register #(.width(32)) register_20 (.D(write_data), .en(_19_out), .Q(register_20_q), .clk(clock));  // open: clr
  Register #(.width(32)) register_21 (.D(write_data), .en(_20_out), .Q(register_21_q), .clk(clock));  // open: clr
  Register #(.width(32)) register_22 (.D(write_data), .en(_21_out), .Q(register_22_q), .clk(clock));  // open: clr
  Register #(.width(32)) register_23 (.D(write_data), .en(_22_out), .Q(register_23_q), .clk(clock));  // open: clr
  Register #(.width(32)) register_24 (.D(write_data), .en(_23_out), .Q(register_24_q), .clk(clock));  // open: clr
  Register #(.width(32)) _24_2 (.D(write_data), .en(_24_out), .Q(from_t8), .clk(clock));  // open: clr
  Register #(.width(32)) _25_2 (
    .D(controlled_buffer_1_out), .en(controlled_buffer_2_out), .Q(from_t9), .clk(clock));  // open: clr
  Register #(.width(32)) _26_2 (.D(write_data), .en(_26_out), .Q(_26_2_q), .clk(clock));  // open: clr
  Register #(.width(32)) _27_2 (.D(write_data), .en(_27_out), .Q(_27_2_q), .clk(clock));  // open: clr
  Register #(.width(32)) _28_2 (.D(write_data), .en(_28_out), .Q(_28_2_q), .clk(clock));  // open: clr
  Register #(.width(32)) _29_2 (.D(write_data), .en(_29_out), .Q(_29_2_q), .clk(clock));  // open: clr
  Register #(.width(32)) _30_2 (.D(write_data), .en(_30_out), .Q(_30_2_q), .clk(clock));  // open: clr
  Register #(.width(32)) _31_2 (.D(write_data), .en(_31_out), .Q(_31_2_q), .clk(clock));  // open: clr
  Multiplexer #(.select(5), .width(32)) multiplexer_1 (
    .in0(register_1_q), .in1(register_2_q), .in2(register_3_q), .in3(register_4_q), .in4(register_5_q),
    .in5(register_6_q), .in6(register_7_q), .in7(register_8_q), .in8(register_9_q), .in9(register_10_q),
    .in10(register_11_q), .in11(register_12_q), .in12(register_13_q), .in13(register_14_q),
    .in14(register_15_q), .in15(register_16_q), .in16(register_17_q), .in17(register_18_q),
    .in18(register_19_q), .in19(register_20_q), .in20(register_21_q), .in21(register_22_q),
    .in22(register_23_q), .in23(register_24_q), .in24(from_t8), .in25(from_t9), .in26(_26_2_q),
    .in27(_27_2_q), .in28(_28_2_q), .in29(_29_2_q), .in30(_30_2_q), .in31(_31_2_q), .out(read_data_1),
    .sel(read_register_1));  // open: en
  Multiplexer #(.select(5), .width(32)) multiplexer_2 (
    .in0(register_1_q), .in1(register_2_q), .in2(register_3_q), .in3(register_4_q), .in4(register_5_q),
    .in5(register_6_q), .in6(register_7_q), .in7(register_8_q), .in8(register_9_q), .in9(register_10_q),
    .in10(register_11_q), .in11(register_12_q), .in12(register_13_q), .in13(register_14_q),
    .in14(register_15_q), .in15(register_16_q), .in16(register_17_q), .in17(register_18_q),
    .in18(register_19_q), .in19(register_20_q), .in20(register_21_q), .in21(register_22_q),
    .in22(register_23_q), .in23(register_24_q), .in24(from_t8), .in25(from_t9), .in26(_26_2_q),
    .in27(_27_2_q), .in28(_28_2_q), .in29(_29_2_q), .in30(_30_2_q), .in31(_31_2_q), .out(read_data_2),
    .sel(read_register_2));  // open: en
endmodule
