// Logisim project lab06part2.circ..circ as structural Verilog: 1 circuit, main circuit main
module main (
  input  in_1,
  input  [7:0] A,
  input  [7:0] B,
  input  Operation,
  output [7:0] Adder_probe,
  output [7:0] Result,
  output [7:0] Subtractor_probe
);

  Adder adder_1 (.a(A), .b(B), .out(Adder_probe), .cin(in_1));  // open: cout
  Subtractor subtractor_1 (.a(A), .b(B), .out(Subtractor_probe), .bin(in_1));  // open: bout
  Multiplexer #(.width(8), .enable("false")) multiplexer_1 (
    .in0(Adder_probe), .in1(Subtractor_probe), .out(Result), .sel(Operation));
endmodule
