// Logisim project lab08.circ as structural Verilog: 3 circuits, main circuit main
module main (
  input  Ainvert,
  input  CarryIn,
  input  Binvert,
  input  [1:0] Operation,
  input  a,
  input  b,
  input  Less,
  output Result,
  output CarryOut,
  output Set
);

  wire and_1_out, multiplexer_1_out, multiplexer_2_out, not_1_out, not_2_out, or_1_out;

  not not_1 (not_1_out, a);
  Multiplexer #(.enable("false")) multiplexer_1 (.in0(a), .in1(not_1_out), .out(multiplexer_1_out), .sel(Ainvert));
  not not_2 (not_2_out, b);
  Multiplexer #(.enable("false")) multiplexer_2 (.in0(b), .in1(not_2_out), .out(multiplexer_2_out), .sel(Binvert));
  and and_1 (and_1_out, multiplexer_1_out, multiplexer_2_out);
  or or_1 (or_1_out, multiplexer_1_out, multiplexer_2_out);
  Adder #(.width(1)) adder_1 (.a(multiplexer_1_out), .b(multiplexer_2_out), .out(Set), .cin(CarryIn), .cout(CarryOut));
  Multiplexer #(.select(2), .enable("false")) multiplexer_3 (
    .in0(and_1_out), .in1(or_1_out), .in2(Set), .in3(Less), .out(Result), .sel(Operation));
endmodule

module ALU (
  input  [7:0] A,
  input  Ainvert,
  input  Bnegate,
  input  [1:0] Operation,
  input  [7:0] B,
  output [7:0] Result,
  output Zero,
  output Overflow
);

  wire main_1_carryout, main_2_carryout, main_3_carryout, main_4_carryout, main_5_carryout, main_6_carryout,
       main_7_carryout, main_8_set, or_1_out;

  main main_1 (
    .a(A[0]), .b(B[0]), .Less(main_8_set), .Result(Result[0]), .Ainvert(Ainvert), .Binvert(Bnegate),
    .CarryIn(Bnegate), .Operation(Operation), .CarryOut(main_1_carryout));  // open: Set
  main main_2 (
    .a(A[1]), .b(B[1]), .Less(1'b0), .Result(Result[1]), .Ainvert(Ainvert), .Binvert(Bnegate),
    .CarryIn(main_1_carryout), .Operation(Operation), .CarryOut(main_2_carryout));  // open: Set
  main main_3 (
    .a(A[2]), .b(B[2]), .Less(1'b0), .Result(Result[2]), .Ainvert(Ainvert), .Binvert(Bnegate),
    .CarryIn(main_2_carryout), .Operation(Operation), .CarryOut(main_3_carryout));  // open: Set
  main main_4 (
    .a(A[3]), .b(B[3]), .Less(1'b0), .Result(Result[3]), .Ainvert(Ainvert), .Binvert(Bnegate),
    .CarryIn(main_3_carryout), .Operation(Operation), .CarryOut(main_4_carryout));  // open: Set
  main main_5 (
    .a(A[4]), .b(B[4]), .Less(1'b0), .Result(Result[4]), .Ainvert(Ainvert), .Binvert(Bnegate),
    .CarryIn(main_4_carryout), .Operation(Operation), .CarryOut(main_5_carryout));  // open: Set
  main main_6 (
    .a(A[5]), .b(B[5]), .Less(1'b0), .Result(Result[5]), .Ainvert(Ainvert), .Binvert(Bnegate),
    .CarryIn(main_5_carryout), .Operation(Operation), .CarryOut(main_6_carryout));  // open: Set
  main main_7 (
    .a(A[6]), .b(B[6]), .Less(1'b0), .Result(Result[6]), .Ainvert(Ainvert), .Binvert(Bnegate),
    .CarryIn(main_6_carryout), .Operation(Operation), .CarryOut(main_7_carryout));  // open: Set
  main main_8 (
    .a(A[7]), .b(B[7]), .Less(1'b0), .Result(Result[7]), .Set(main_8_set), .Ainvert(Ainvert),
    .Binvert(Bnegate), .CarryIn(main_7_carryout), .Operation(Operation), .CarryOut(Overflow));
  or or_1 (or_1_out, Result[0], Result[1], Result[2], Result[7]);
  not not_1 (Zero, or_1_out);
endmodule

module ALU1 (
  input  [1:0] in_1,
  input  in_2,
  input  in_3,
  input  [7:0] A,
  input  [7:0] B,
  output [7:0] Result,
  output Zero,
  output Overflow
);

  ALU alu_1 (
    .A(A), .B(B), .Ainvert(in_2), .Bnegate(in_3), .Operation(in_1), .Result(Result), .Zero(Zero),
    .Overflow(Overflow));
endmodule
