// Logisim project lab10.circ as structural Verilog: 3 circuits, main circuit main
module main (
);

  wire not_2_out, not_3_out;
  wire [0:0] not_1_out;
  wire [3:0] fields_1_op;
  wire [7:0] A_q, adder_1_out, alu_1_result, B_q, fields_1_imm, PC_q, rom_1_data;

  Register PC (.D(adder_1_out), .en(1'b1), .Q(PC_q));  // open: clk, clr
  Adder adder_1 (.a(PC_q), .out(adder_1_out), .cin(1'b1));  // open: b, cout
  ROM rom_1 (.addr(PC_q), .data(rom_1_data), .sel(1'b1));
  Register A (.D(rom_1_data), .Q(A_q));  // open: en, clk, clr
  Register B (.D(rom_1_data), .Q(B_q));  // open: en, clk, clr
  Fields fields_1 (.OP(fields_1_op), .imm(fields_1_imm));  // open: Input
  ALU alu_1 (
    .a(A_q), .b(B_q), .Op({fields_1_op[0], not_1_out[0]}), .Result(alu_1_result));  // open: BInvert, CarryIn, CarryOut
  Multiplexer #(.width(8), .enable("false")) multiplexer_1 (.in0(alu_1_result), .in1(fields_1_imm));  // open: out, sel
  not not_1 (not_1_out[0], fields_1_op[1]);
  not not_2 (not_2_out, fields_1_op[2]);
  not not_3 (not_3_out, fields_1_op[1]);
  // AND_Gate and_1 has open pins: in0=not_2_out, in1=not_3_out, out=open

  // Notes on the sheet:
  //   SetMux
endmodule

module ALU (
  input  BInvert,
  input  CarryIn,
  input  [1:0] Op,
  input  [7:0] a,
  input  [7:0] b,
  output [7:0] Result,
  output CarryOut
);

  wire [7:0] adder_1_out, and_1_out, multiplexer_1_out, not_1_out, or_1_out;

  assign not_1_out = ~b;  // NOT_Gate not_1, 8 bits wide
  Multiplexer #(.width(8), .enable("false")) multiplexer_1 (
    .in0(b), .in1(not_1_out), .out(multiplexer_1_out), .sel(BInvert));
  assign and_1_out = a;  // AND_Gate and_1, 8 bits wide AND_Gate
  assign or_1_out = a;  // OR_Gate or_1, 8 bits wide OR_Gate
  Adder adder_1 (.a(a), .b(multiplexer_1_out), .out(adder_1_out), .cin(CarryIn), .cout(CarryOut));
  Multiplexer #(.select(2), .width(8), .enable("false")) multiplexer_2 (
    .in0(adder_1_out), .in1(adder_1_out), .in2(and_1_out), .in3(or_1_out), .out(Result), .sel(Op));
endmodule

module Fields (
  input  [15:0] Input,
  output [3:0] OP,
  output [7:0] imm
);

  Register #(.width(1)) Register (.D(Input[4]));  // open: en, Q, clk, clr

  assign imm = Input[12:5];
  assign OP = Input[3:0];
endmodule
